# Fritzing sketch AStar_32u4_battery_discharger (saved by Fritzing 0.8.5b)
breadboards: 1

parts:
  R1 = Resistor [tolerance=±5% resistance=220 package=THT]
  R2 = Resistor [tolerance=±5% resistance=220 package=THT]
  R3 = Resistor [tolerance=±5% resistance=220 package=THT]
  Q1 = MOSFET-NCHANNEL [package=sot323]
  U1 = LIPO-1000mAh [package=lipo-1000]
  Part1 = Arduino Leonardo (Rev3b)
  R4 = Resistor [tolerance=±5% resistance=220 package=THT]

nets:
  N1: R1.Pin_0, R2.Pin_0, R3.Pin_0, U1.+, Part1.D11_PWM
  N2: R1.Pin_1, R2.Pin_1, R3.Pin_1, Q1.D, Part1.D10_PWM/A10
  N3: Q1.G, Part1.D12/A11, R4.Pin_0
  N4: Q1.S, U1.-, Part1.GND, R4.Pin_1

notes:
  These resistors are actually about 100 Ohm each, but that's configurable in the octave code
  The MOSFET is for disconnecting the battery after the test is complete
  Dual ADCs for properly measuring the voltage drop
  (hint: one of them should be zero but isn't)
  The battery in this sketch is actually a very good one. Its measured capacity was 1183 mAh.
  Fun fact: This is my first circuit ever that uses a MOSFET. It felt like discovering LEDs all over again.
  10k pulldown between the gate pin and GND, this prevents the gate from floating and randomly turning on the MOSFET by itself
